# Fritzing sketch able-buttons (saved by Fritzing 1.0.2b)
breadboards: 1

parts:
  NANO1 = Arduino Nano (Rev3.0)
  S1 = Pushbutton [package=THT]
  S2 = Pushbutton [package=THT]

nets:
  N1: NANO1.GND, S1.leg0, S2.leg0
  N2: NANO1.D2, S1.leg1
  N3: NANO1.D3, S2.leg1
